// Logisim project Data Path.circ as structural Verilog
module R_file (
  input  [31:0] in_1,
  input  [3:0] Rs,
  input  [3:0] Rt,
  input  [3:0] Rd,
  input  RegW,
  input  CLK,
  input  in_7,
  output [31:0] BusY,
  output [31:0] BusZ
);

  wire and_1_out, and_2_out, and_3_out, and_4_out, and_5_out, and_6_out, and_7_out, and_8_out, and_9_out,
       and_10_out, and_11_out, and_12_out, and_13_out, and_14_out, and_15_out, decoder_1_out15,
       decoder_2_out0, decoder_2_out1, decoder_2_out2, decoder_2_out3, decoder_2_out4, decoder_2_out5,
       decoder_2_out6, decoder_2_out7, decoder_2_out8, decoder_2_out9, decoder_2_out10, decoder_2_out11,
       decoder_2_out12, decoder_2_out13, decoder_2_out14, decoder_2_out15, decoder_3_out0, decoder_3_out1,
       decoder_3_out2, decoder_3_out3, decoder_3_out4, decoder_3_out5, decoder_3_out6, decoder_3_out7,
       decoder_3_out8, decoder_3_out9, decoder_3_out10, decoder_3_out11, decoder_3_out12, decoder_3_out13,
       decoder_3_out14, decoder_3_out15, R0, R1, R2, R3, R4, R5, R6, R7, R8, R9, R10, R11, R12, R13, R14;
  wire [31:0] W0, W1, W2, W3, W4, W5, W6, W7, W8, W9, W10, W11, W12, W13, W14;

  Decoder #(.select(4), .enable("false")) decoder_1 (
    .out0(R0), .out1(R1), .out2(R2), .out3(R3), .out4(R4), .out5(R5), .out6(R6), .out7(R7), .out8(R8),
    .out9(R9), .out10(R10), .out11(R11), .out12(R12), .out13(R13), .out14(R14), .out15(decoder_1_out15),
    .sel(Rd));
  Controlled_Buffer #(.width(3)) controlled_buffer_1 (.in(3'b000), .en(decoder_1_out15));  // open: out
  and and_1 (and_1_out, R0, RegW);
  and and_2 (and_2_out, R1, RegW);
  and and_3 (and_3_out, R2, RegW);
  and and_4 (and_4_out, R3, RegW);
  and and_5 (and_5_out, R4, RegW);
  and and_6 (and_6_out, R5, RegW);
  and and_7 (and_7_out, R6, RegW);
  and and_8 (and_8_out, R7, RegW);
  and and_9 (and_9_out, R8, RegW);
  and and_10 (and_10_out, R9, RegW);
  and and_11 (and_11_out, R10, RegW);
  and and_12 (and_12_out, R11, RegW);
  and and_13 (and_13_out, R12, RegW);
  and and_14 (and_14_out, R13, RegW);
  and and_15 (and_15_out, R14, RegW);
  Register #(.width(32)) register_1 (.D(in_1), .en(and_1_out), .Q(W0), .clk(CLK), .clr(in_7));
  Register #(.width(32)) register_2 (.D(in_1), .en(and_2_out), .Q(W1), .clk(CLK), .clr(in_7));
  Register #(.width(32)) register_3 (.D(in_1), .en(and_3_out), .Q(W2), .clk(CLK), .clr(in_7));
  Register #(.width(32)) register_4 (.D(in_1), .en(and_4_out), .Q(W3), .clk(CLK), .clr(in_7));
  Register #(.width(32)) register_5 (.D(in_1), .en(and_5_out), .Q(W4), .clk(CLK), .clr(in_7));
  Register #(.width(32)) register_6 (.D(in_1), .en(and_6_out), .Q(W5), .clk(CLK), .clr(in_7));
  Register #(.width(32)) register_7 (.D(in_1), .en(and_7_out), .Q(W6), .clk(CLK), .clr(in_7));
  Register #(.width(32)) register_8 (.D(in_1), .en(and_8_out), .Q(W7), .clk(CLK), .clr(in_7));
  Register #(.width(32)) register_9 (.D(in_1), .en(and_9_out), .Q(W8), .clk(CLK), .clr(in_7));
  Register #(.width(32)) register_10 (.D(in_1), .en(and_10_out), .Q(W9), .clk(CLK), .clr(in_7));
  Register #(.width(32)) register_11 (.D(in_1), .en(and_11_out), .Q(W10), .clk(CLK), .clr(in_7));
  Register #(.width(32)) register_12 (.D(in_1), .en(and_12_out), .Q(W11), .clk(CLK), .clr(in_7));
  Register #(.width(32)) register_13 (.D(in_1), .en(and_13_out), .Q(W12), .clk(CLK), .clr(in_7));
  Register #(.width(32)) register_14 (.D(in_1), .en(and_14_out), .Q(W13), .clk(CLK), .clr(in_7));
  Register #(.width(32)) register_15 (.D(in_1), .en(and_15_out), .Q(W14), .clk(CLK), .clr(in_7));
  assign BusY = decoder_2_out4 ? W4 : 32'bz;  // Controlled_Buffer controlled_buffer_2
  assign BusY = decoder_2_out5 ? W5 : 32'bz;  // Controlled_Buffer controlled_buffer_3
  assign BusY = decoder_2_out6 ? W6 : 32'bz;  // Controlled_Buffer controlled_buffer_4
  assign BusY = decoder_2_out7 ? W7 : 32'bz;  // Controlled_Buffer controlled_buffer_5
  assign BusY = decoder_2_out8 ? W8 : 32'bz;  // Controlled_Buffer controlled_buffer_6
  assign BusY = decoder_2_out9 ? W9 : 32'bz;  // Controlled_Buffer controlled_buffer_7
  assign BusY = decoder_2_out10 ? W10 : 32'bz;  // Controlled_Buffer controlled_buffer_8
  assign BusY = decoder_2_out11 ? W11 : 32'bz;  // Controlled_Buffer controlled_buffer_9
  assign BusY = decoder_2_out12 ? W12 : 32'bz;  // Controlled_Buffer controlled_buffer_10
  assign BusY = decoder_2_out13 ? W13 : 32'bz;  // Controlled_Buffer controlled_buffer_11
  assign BusY = decoder_2_out14 ? W14 : 32'bz;  // Controlled_Buffer controlled_buffer_12
  assign BusY = decoder_2_out0 ? W0 : 32'bz;  // Controlled_Buffer controlled_buffer_13
  assign BusY = decoder_2_out1 ? W1 : 32'bz;  // Controlled_Buffer controlled_buffer_14
  assign BusY = decoder_2_out2 ? W2 : 32'bz;  // Controlled_Buffer controlled_buffer_15
  assign BusY = decoder_2_out3 ? W3 : 32'bz;  // Controlled_Buffer controlled_buffer_16
  Decoder #(.select(4), .enable("false")) decoder_2 (
    .out0(decoder_2_out0), .out1(decoder_2_out1), .out2(decoder_2_out2), .out3(decoder_2_out3),
    .out4(decoder_2_out4), .out5(decoder_2_out5), .out6(decoder_2_out6), .out7(decoder_2_out7),
    .out8(decoder_2_out8), .out9(decoder_2_out9), .out10(decoder_2_out10), .out11(decoder_2_out11),
    .out12(decoder_2_out12), .out13(decoder_2_out13), .out14(decoder_2_out14), .out15(decoder_2_out15),
    .sel(Rs));
  assign BusY = decoder_2_out15 ? {32{1'b0}} : 32'bz;  // Controlled_Buffer controlled_buffer_17
  Decoder #(.select(4), .enable("false")) decoder_3 (
    .out0(decoder_3_out0), .out1(decoder_3_out1), .out2(decoder_3_out2), .out3(decoder_3_out3),
    .out4(decoder_3_out4), .out5(decoder_3_out5), .out6(decoder_3_out6), .out7(decoder_3_out7),
    .out8(decoder_3_out8), .out9(decoder_3_out9), .out10(decoder_3_out10), .out11(decoder_3_out11),
    .out12(decoder_3_out12), .out13(decoder_3_out13), .out14(decoder_3_out14), .out15(decoder_3_out15),
    .sel(Rt));
  assign BusZ = decoder_3_out1 ? W1 : 32'bz;  // Controlled_Buffer controlled_buffer_18
  assign BusZ = decoder_3_out0 ? W0 : 32'bz;  // Controlled_Buffer controlled_buffer_19
  assign BusZ = decoder_3_out2 ? W2 : 32'bz;  // Controlled_Buffer controlled_buffer_20
  assign BusZ = decoder_3_out3 ? W3 : 32'bz;  // Controlled_Buffer controlled_buffer_21
  assign BusZ = decoder_3_out4 ? W4 : 32'bz;  // Controlled_Buffer controlled_buffer_22
  assign BusZ = decoder_3_out5 ? W5 : 32'bz;  // Controlled_Buffer controlled_buffer_23
  assign BusZ = decoder_3_out6 ? W6 : 32'bz;  // Controlled_Buffer controlled_buffer_24
  assign BusZ = decoder_3_out7 ? W7 : 32'bz;  // Controlled_Buffer controlled_buffer_25
  assign BusZ = decoder_3_out8 ? W8 : 32'bz;  // Controlled_Buffer controlled_buffer_26
  assign BusZ = decoder_3_out9 ? W9 : 32'bz;  // Controlled_Buffer controlled_buffer_27
  assign BusZ = decoder_3_out10 ? W10 : 32'bz;  // Controlled_Buffer controlled_buffer_28
  assign BusZ = decoder_3_out11 ? W11 : 32'bz;  // Controlled_Buffer controlled_buffer_29
  assign BusZ = decoder_3_out12 ? W12 : 32'bz;  // Controlled_Buffer controlled_buffer_30
  assign BusZ = decoder_3_out13 ? W13 : 32'bz;  // Controlled_Buffer controlled_buffer_31
  assign BusZ = decoder_3_out14 ? W14 : 32'bz;  // Controlled_Buffer controlled_buffer_32
  assign BusZ = decoder_3_out15 ? {32{1'b0}} : 32'bz;  // Controlled_Buffer controlled_buffer_33

  // Other names for the same wires on the sheet: OUT_0[31:0] = BusY; OUT_1[31:0] = BusY; OUT_2[31:0] = BusY;
  //   OUT_3[31:0] = BusY; OUT_4[31:0] = BusY; OUT_5[31:0] = BusY; OUT_6[31:0] = BusY; OUT_7[31:0] = BusY;
  //   OUT_8[31:0] = BusY; OUT_9[31:0] = BusY; OUT_10[31:0] = BusY; OUT_11[31:0] = BusY; OUT_12[31:0] = BusY;
  //   OUT_13[31:0] = BusY; OUT_14[31:0] = BusY
endmodule

module Main_Control_Unit (
  input  [5:0] Opcode,
  input  Round2,
  input  in_3,
  output [1:0] ALUop,
  output [1:0] WritebData,
  output MemR,
  output MemWrite,
  output [1:0] ALUSrc,
  output EXop,
  output RegWrite,
  output Source,
  output [1:0] Rdist
);

  wire [1:0] multiplexer_1_out;
  wire [3:0] OP;

  ROM #(.dataWidth(13)) rom_1 (
    .addr({in_3, Round2, Opcode}),
    .data({Rdist, Source, RegWrite, EXop, ALUSrc, MemWrite, MemR, WritebData, ALUop}));  // open: sel
  Multiplexer #(.select(4), .width(2), .enable("false")) multiplexer_1 (
    .in0(2'b00), .in1(2'b01), .in2(2'b10), .in3(2'b11), .in4(2'b00), .in5(2'b01), .in6(2'b01), .in7(2'b01),
    .in8(2'b01), .in9(2'b01), .in10(2'b11), .in11(2'b11), .in12(2'b11), .out(multiplexer_1_out), .sel(OP));  // open: in13, in14, in15

  // Notes on the sheet:
  //   1010 0000 1000
  //   contents of rom_1 (hex, n*v repeats v):
  //   600 601 602 603 740 741 755 161 755 161 83 83 83 0 0 a08 56*0 13d5 11e1
endmodule

module Pc (
  input  [5:0] OpCode,
  input  [31:0] X,
  output [2:0] Pcs,
  output Gratter,
  output Zero,
  output Smaller
);

  ROM #(.addrWidth(6), .dataWidth(3)) rom_1 (.addr(OpCode), .data(Pcs));  // open: sel
  ROM #(.addrWidth(10), .dataWidth(3)) rom_2 ();  // open: addr, data, sel
  ROM #(.addrWidth(6), .dataWidth(3)) rom_3 ();  // open: addr, data, sel
  Comparator #(.width(32)) comparator_1 (.a(X), .b({32{1'b0}}), .gt(Gratter), .eq(Zero), .lt(Smaller));

  // Notes on the sheet:
  //   contents of rom_1 (hex, n*v repeats v):
  //   8*0 7 7 1 2 3 4 5 6
  //   contents of rom_2 (hex, n*v repeats v):
  //   13*0 2 3 3 58*0 1 64*0 1 124*0 4 4 0 0 1
  //   contents of rom_3 (hex, n*v repeats v):
  //   8*0 7 7 1 2 3 4 5 6 15*0 6
endmodule

module datapath (
  input  in_1,
  input  in_2,
  output [5:0] out_3,
  output [3:0] out_4,
  output [3:0] out_5,
  output [31:0] out_6
);

  wire B, C, CLK_out, comparator_1_eq, comparator_2_eq, comparator_3_eq, comparator_4_eq, comparator_4_gt,
       comparator_4_lt, eq, ex_mem_1_mem_read_2, ex_mem_1_mem_write_2, ex_mem_1_we_2, EXop, G_Zero,
       id_mem_1_mem_red_2, id_mem_1_mem_write_2, id_mem_1_we_2, kill, L_Zero, ldw_2_round2_load,
       ldw_2_round2_store, LWD, main_control_unit_1_memr, main_control_unit_1_memwrite,
       main_control_unit_1_regwrite, mem_wb_1_wb_2, MemR, MemWrite, multiplexer_18_out, or_1_out, or_2_out,
       RegWrite, Round2, Source, stall, SWD, Zero;
  wire [1:0] ALU_Src, ex_mem_1_wb_2, Forward_A, Forward_B, id_mem_1_alu_signal_2, id_mem_1_wb_2,
       main_control_unit_1_aluop, main_control_unit_1_alusrc, main_control_unit_1_writebdata, Rdist, WB;
  wire [2:0] Pcs;
  wire [3:0] adder_5_out, ex_mem_1_rd_2, id_mem_1_rd_2, multiplexer_19_out, Rd, rom_1_data_2, rom_1_data_3,
       rom_1_data_4, Rt, RZ;
  wire [5:0] multiplexer_4_out, multiplexer_13_out, multiplexer_14_out, multiplexer_15_out, OP1;
  wire [13:0] Imm14, rom_1_data;
  wire [19:0] adder_2_out, adder_3_out, bit_extender_1_out, bit_extender_2_out, bit_extender_3_out,
       bit_extender_5_out, Branch, ex_mem_1_pc_2, id_mem_1_pc_2, multiplexer_1_out, multiplexer_2_out,
       multiplexer_3_out, multiplexer_5_out, multiplexer_11_out, multiplexer_12_out, PC, PC_1;
  wire [31:0] alu_1_alu_result, bit_extender_4_out, bit_extender_6_out, Busx, ex_mem_1_data_2,
       ex_mem_1_result_2, id_mem_1_data_2, id_mem_1_inp_1_2, id_mem_1_inp_2_2, if_mem_1_inst_2, IMM___1,
       multiplexer_16_out, multiplexer_17_out, multiplexer_21_out, multiplexer_22_out, multiplexer_23_out,
       multiplexer_24_out, r_file_1_busz, ram_1_data;

  // Probe on out_3
  // Probe on bit_extender_1_out
  // Probe on Imm14
  // Probe on Round2
  assign bit_extender_1_out = {{6{Imm14[13]}}, Imm14};  // Bit_Extender bit_extender_1
  // Probe on PC
  Multiplexer #(.width(20), .enable("false")) multiplexer_1 (
    .in0(PC_1), .in1(Branch), .out(multiplexer_1_out), .sel(comparator_4_lt));
  assign bit_extender_2_out = {{16{1'b0}}, out_4};  // Bit_Extender bit_extender_2
  assign bit_extender_3_out = {{6{Imm14[13]}}, Imm14};  // Bit_Extender bit_extender_3
  Main_Control_Unit main_control_unit_1 (
    .Opcode(out_3), .WritebData(main_control_unit_1_writebdata), .MemR(main_control_unit_1_memr),
    .MemWrite(main_control_unit_1_memwrite), .ALUSrc(main_control_unit_1_alusrc), .EXop(EXop),
    .RegWrite(main_control_unit_1_regwrite), .Source(Source), .ALUop(main_control_unit_1_aluop),
    .Rdist(Rdist), .Round2(Round2), .in_3(in_2));
  Adder #(.width(20)) adder_1 (.a(bit_extender_1_out), .b(PC), .out(Branch));  // open: cin, cout
  Multiplexer #(.width(20), .enable("false")) multiplexer_2 (
    .in0(PC_1), .in1(Branch), .out(multiplexer_2_out), .sel(comparator_4_gt));
  // Probe on Branch
  Multiplexer #(.width(20), .enable("false")) multiplexer_3 (
    .in0(PC_1), .in1(Branch), .out(multiplexer_3_out), .sel(comparator_4_eq));
  Adder #(.width(20)) adder_2 (.a(bit_extender_2_out), .b(PC), .out(adder_2_out));  // open: cin, cout
  Adder #(.width(20)) adder_3 (.a(bit_extender_3_out), .b(PC), .out(adder_3_out));  // open: cin, cout
  // Probe on main_control_unit_1_aluop
  or or_1 (or_1_out, SWD, LWD);
  Multiplexer #(.width(6), .enable("false")) multiplexer_4 (
    .in0(OP1), .out(multiplexer_4_out), .sel(stall));  // open: in1
  Multiplexer #(.width(20), .enable("false")) multiplexer_5 (
    .in0(PC), .in1(PC_1), .out(multiplexer_5_out), .sel(or_1_out));
  // Probe on Pcs
  LDW ldw_1 (.Clock(CLK_out), .in_1(multiplexer_4_out), .Round2_Load(LWD), .Round2_Store(SWD));
  Multiplexer #(.width(2), .enable("false")) multiplexer_6 (
    .in0(main_control_unit_1_writebdata), .in1(2'b00), .out(WB), .sel(stall));
  Multiplexer #(.enable("false")) multiplexer_7 (.in0(main_control_unit_1_memr), .in1(1'b0), .out(MemR), .sel(stall));
  Multiplexer #(.enable("false")) multiplexer_8 (
    .in0(main_control_unit_1_memwrite), .in1(1'b0), .out(MemWrite), .sel(stall));
  Multiplexer #(.width(2), .enable("false")) multiplexer_9 (
    .in0(main_control_unit_1_alusrc), .in1(2'b00), .out(ALU_Src), .sel(stall));
  Multiplexer #(.enable("false")) multiplexer_10 (
    .in0(main_control_unit_1_regwrite), .in1(1'b0), .out(RegWrite), .sel(stall));
  Multiplexer #(.select(3), .width(20), .enable("false")) multiplexer_11 (
    .in0(PC_1), .in1(multiplexer_3_out), .in2(multiplexer_2_out), .in3(multiplexer_1_out), .in4(adder_2_out),
    .in5(adder_3_out), .in6(adder_3_out), .in7(multiplexer_5_out), .out(multiplexer_11_out), .sel(Pcs));
  Multiplexer #(.width(20), .enable("false")) multiplexer_12 (
    .in0(multiplexer_11_out), .in1(PC), .out(multiplexer_12_out), .sel(stall));
  Register #(.width(20)) u_PC (.D(multiplexer_12_out), .en(1'b1), .Q(PC), .clk(CLK_out), .clr(in_1));
  Multiplexer #(.width(6), .enable("false")) multiplexer_13 (
    .in0(OP1), .in1(out_3), .out(multiplexer_13_out), .sel(stall));
  Adder #(.width(20)) adder_4 (.a(PC), .b(20'h1), .out(PC_1));  // open: cin, cout
  Multiplexer #(.width(6), .enable("false")) multiplexer_14 (
    .in0(multiplexer_13_out), .in1(out_3), .out(multiplexer_14_out), .sel(kill));
  Multiplexer #(.width(6), .enable("false")) multiplexer_15 (
    .in0(multiplexer_14_out), .in1(out_3), .out(multiplexer_15_out), .sel(or_2_out));
  Multiplexer #(.width(32), .enable("false")) multiplexer_16 (
    .in0(multiplexer_17_out), .in1({32{1'b1}}), .out(multiplexer_16_out), .sel(kill));
  ROM #(.addrWidth(20), .dataWidth(32)) rom_1 (
    .addr(PC), .data({OP1, rom_1_data_4, rom_1_data_3, rom_1_data_2, rom_1_data}));  // open: sel
  Pc pc_2 (.X(Busx), .Smaller(L_Zero), .Gratter(G_Zero), .Zero(Zero), .OpCode(multiplexer_15_out), .Pcs(Pcs));
  Multiplexer #(.width(32), .enable("false")) multiplexer_17 (
    .in0({OP1, rom_1_data_4, rom_1_data_3, rom_1_data_2, rom_1_data}), .in1(if_mem_1_inst_2),
    .out(multiplexer_17_out), .sel(stall));
  IF_Mem if_mem_1 (.Inst(multiplexer_16_out), .CLK(CLK_out), .Inst_2(if_mem_1_inst_2), .in_4(in_1));  // open: Pc_2, Pc
  Comparator #(.width(6)) comparator_1 (.a(OP1), .b(6'b001100), .eq(comparator_1_eq));  // open: gt, lt
  Comparator #(.width(6)) comparator_2 (.a(OP1), .b(6'b001011), .eq(comparator_2_eq));  // open: gt, lt
  Comparator #(.width(6)) comparator_3 (.a(OP1), .b(6'b001010), .eq(comparator_3_eq));  // open: gt, lt
  or or_2 (or_2_out, comparator_1_eq, comparator_2_eq, comparator_3_eq);
  // Probe on if_mem_1_inst_2
  Decode_Stage decode_stage_1 (
    .Instruction(if_mem_1_inst_2), .out_2(out_3), .out_3(Rd), .out_4(out_4), .out_5(Rt), .out_6(Imm14));
  Multiplexer #(.enable("false")) multiplexer_18 (.in0(CLK_out), .out(multiplexer_18_out), .sel(stall));  // open: in1
  Adder #(.width(4)) adder_5 (.a(Rd), .b(4'b0001), .out(adder_5_out));  // open: cin, cout
  // Probe on out_4
  LDW ldw_2 (
    .Clock(multiplexer_18_out), .in_1(out_3), .Round2_Load(ldw_2_round2_load),
    .Round2_Store(ldw_2_round2_store));
  // Probe on Imm14
  // Probe on multiplexer_19_out
  assign bit_extender_4_out = {{18{Imm14[13]}}, Imm14};  // Bit_Extender bit_extender_4
  Multiplexer #(.width(4), .enable("false")) multiplexer_19 (
    .in0(RZ), .in1(Rt), .out(multiplexer_19_out), .sel(Source));
  Multiplexer #(.select(2), .width(4), .enable("false")) multiplexer_20 (
    .in0(Rd), .in1(4'b1110), .in2(adder_5_out), .out(RZ), .sel(Rdist));  // open: in3
  // Probe on multiplexer_19_out
  or or_3 (Round2, ldw_2_round2_load, ldw_2_round2_store);
  Adder #(.width(32)) adder_6 (.a(32'h1), .b(bit_extender_4_out), .out(IMM___1));  // open: cin, cout
  // Probe on bit_extender_4_out
  R_file r_file_1 (
    .Rs(out_4), .Rt(multiplexer_19_out), .Rd(out_5), .RegW(mem_wb_1_wb_2), .CLK(CLK_out),
    .BusZ(r_file_1_busz), .BusY(Busx), .in_1(out_6), .in_7(in_1));
  Clock CLK (.out(CLK_out));
  // Probe on multiplexer_23_out
  Multiplexer #(.select(2), .width(32), .enable("false")) multiplexer_21 (
    .in0(Busx), .in1(alu_1_alu_result), .in2(multiplexer_24_out), .in3(out_6), .out(multiplexer_21_out),
    .sel(Forward_A));
  // Probe on ALU_Src
  Multiplexer #(.select(2), .width(32), .enable("false")) multiplexer_22 (
    .in0(multiplexer_23_out), .in1(bit_extender_4_out), .in2({32{1'b0}}), .in3(IMM___1),
    .out(multiplexer_22_out), .sel(ALU_Src));
  // Probe on multiplexer_22_out
  Comparator #(.width(32)) comparator_4 (
    .a(multiplexer_21_out), .b(multiplexer_22_out), .gt(comparator_4_gt), .eq(comparator_4_eq),
    .lt(comparator_4_lt));
  Multiplexer #(.select(2), .width(32), .enable("false")) multiplexer_23 (
    .in0(r_file_1_busz), .in1(alu_1_alu_result), .in2(multiplexer_24_out), .in3(out_6),
    .out(multiplexer_23_out), .sel(Forward_B));
  // Probe on id_mem_1_rd_2
  ID_Mem id_mem_1 (
    .Rd(RZ), .WB(WB), .MEM_Red(MemR), .MEM_Write(MemWrite), .inp_1(multiplexer_21_out),
    .inp_2(multiplexer_22_out), .Alu_Signal(main_control_unit_1_aluop), .WE(RegWrite), .CLK(CLK_out),
    .Rd_2(id_mem_1_rd_2), .WB_2(id_mem_1_wb_2), .MEM_Red_2(id_mem_1_mem_red_2),
    .MEM_Write_2(id_mem_1_mem_write_2), .inp_1_2(id_mem_1_inp_1_2), .inp_2_2(id_mem_1_inp_2_2),
    .Alu_Signal_2(id_mem_1_alu_signal_2), .WE_2(id_mem_1_we_2), .Data(multiplexer_23_out),
    .Data_2(id_mem_1_data_2), .Pc(PC), .Pc_2(id_mem_1_pc_2), .in_12(in_1));
  // Probe on multiplexer_21_out
  // Probe on id_mem_1_rd_2
  // Probe on id_mem_1_inp_2_2
  Forwarding_Unit forwarding_unit_1 (
    .Rs(out_4), .Rd_EX(id_mem_1_rd_2), .Rd_MEM(ex_mem_1_rd_2), .Rd_WB(out_5), .EX_WE(id_mem_1_we_2),
    .Mem_WE(ex_mem_1_we_2), .WB_WE(mem_wb_1_wb_2), .Forward(Forward_A));
  // Probe on id_mem_1_inp_1_2
  ALU alu_1 (
    .A_input(id_mem_1_inp_1_2), .B_input(id_mem_1_inp_2_2), .OP(id_mem_1_alu_signal_2), .out_4(C),
    .out_5(eq), .out_6(B), .ALU_Result(alu_1_alu_result));
  // Probe on Forward_A
  // Probe on id_mem_1_alu_signal_2
  // Probe on id_mem_1_data_2
  // Probe on ex_mem_1_rd_2
  // Probe on alu_1_alu_result
  // Probe on id_mem_1_rd_2
  EX_Mem ex_mem_1 (
    .Rd(id_mem_1_rd_2), .WE(id_mem_1_we_2), .Mem_Read(id_mem_1_mem_red_2), .Mem_Write(id_mem_1_mem_write_2),
    .Result(alu_1_alu_result), .C(C), .eq(eq), .B(B), .WB(id_mem_1_wb_2), .CLK(CLK_out),
    .Rd_2(ex_mem_1_rd_2), .WE_2(ex_mem_1_we_2), .Mem_Read_2(ex_mem_1_mem_read_2),
    .Mem_Write_2(ex_mem_1_mem_write_2), .Result_2(ex_mem_1_result_2), .WB_2(ex_mem_1_wb_2),
    .Data_2(ex_mem_1_data_2), .Data(id_mem_1_data_2), .Pc(id_mem_1_pc_2), .Pc_2(ex_mem_1_pc_2), .in_13(in_1));  // open: C_2, eq_2, B_2
  Hazard_Detection hazard_detection_1 (
    .MEMRead_EX(id_mem_1_mem_red_2), .FA(Forward_A), .FB(Forward_B), .in_4(out_3), .in_5(comparator_4_eq),
    .in_6(comparator_4_gt), .in_7(comparator_4_lt), .Stall(stall), .out_9(kill));
  // Probe on ex_mem_1_result_2
  // Probe on ex_mem_1_rd_2
  Forwarding_Unit forwarding_unit_2 (
    .Rs(multiplexer_19_out), .Rd_EX(id_mem_1_rd_2), .Rd_MEM(ex_mem_1_rd_2), .Rd_WB(out_5),
    .EX_WE(id_mem_1_we_2), .Mem_WE(ex_mem_1_we_2), .WB_WE(mem_wb_1_wb_2), .Forward(Forward_B));
  // Probe on Forward_B
  // Probe on stall
  // Probe on ex_mem_1_result_2
  // Probe on ex_mem_1_data_2
  // Probe on ex_mem_1_wb_2
  Bit_Extender #(.in_width(32), .out_width(20)) bit_extender_5 (.in(ex_mem_1_result_2), .out(bit_extender_5_out));
  // Probe on out_6
  // Probe on ex_mem_1_rd_2
  RAM #(.addrWidth(20), .dataWidth(32), .bus("separate")) ram_1 (
    .addr(bit_extender_5_out), .din(ex_mem_1_data_2), .data(ram_1_data), .str(ex_mem_1_mem_write_2),
    .clk(CLK_out), .ld(ex_mem_1_mem_read_2), .clr(in_1));  // open: sel
  assign bit_extender_6_out = {{12{ex_mem_1_pc_2[19]}}, ex_mem_1_pc_2};  // Bit_Extender bit_extender_6
  // Probe on ex_mem_1_wb_2
  Multiplexer #(.select(2), .width(32), .enable("false")) multiplexer_24 (
    .in0(ex_mem_1_result_2), .in1(ram_1_data), .in2(bit_extender_6_out), .in3({32{1'b0}}),
    .out(multiplexer_24_out), .sel(ex_mem_1_wb_2));
  // Probe on multiplexer_24_out
  Mem_WB mem_wb_1 (
    .Rd(ex_mem_1_rd_2), .Data(multiplexer_24_out), .WB(ex_mem_1_we_2), .Clk_prime(CLK_out), .Rd_2(out_5),
    .Data_2(out_6), .WB_2(mem_wb_1_wb_2), .in_5(in_1));

  // Other names for the same wires on the sheet: CC = in_1; OP[5:0] = out_3; Rs[3:0] = out_4

  // Notes on the sheet:
  //   Lw R0 , 5
  //   LW R1 , 7
  //   ADD R5 , R0 ,R1
  //   NOP
  //   contents of rom_1 (hex, n*v repeats v):
  //   20840000 14c80001 24840004 280c0006
endmodule

module ALU (
  input  [31:0] A_input,
  input  [31:0] B_input,
  input  [1:0] OP,
  output out_4,
  output out_5,
  output out_6,
  output [31:0] ALU_Result
);

  wire comparator_1_eq, comparator_1_gt, comparator_1_lt;
  wire [31:0] adder_1_out, bit_extender_1_out, bit_extender_2_out, bit_extender_3_out,
       controlled_buffer_1_out, or_1_out, subtractor_1_out;

  // Probe on A_input
  Adder #(.width(32)) adder_1 (.a(A_input), .b(B_input), .out(adder_1_out), .cin(1'b0));  // open: cout
  Subtractor #(.width(32)) subtractor_1 (.a(A_input), .b(B_input), .out(subtractor_1_out), .bin(1'b0));  // open: bout
  Comparator #(.width(32)) comparator_1 (
    .a(A_input), .b(B_input), .gt(comparator_1_gt), .eq(comparator_1_eq), .lt(comparator_1_lt));
  assign bit_extender_1_out = {{31{1'b1}}, 1'b1};  // Bit_Extender bit_extender_1
  assign bit_extender_2_out = {{31{1'b0}}, 1'b0};  // Bit_Extender bit_extender_2
  assign bit_extender_3_out = {{31{1'b0}}, 1'b1};  // Bit_Extender bit_extender_3
  assign controlled_buffer_1_out = comparator_1_lt ? bit_extender_1_out : 32'bz;  // Controlled_Buffer controlled_buffer_1
  assign controlled_buffer_1_out = comparator_1_eq ? bit_extender_2_out : 32'bz;  // Controlled_Buffer controlled_buffer_2
  assign controlled_buffer_1_out = comparator_1_gt ? bit_extender_3_out : 32'bz;  // Controlled_Buffer controlled_buffer_3
  Comparator #(.width(32)) comparator_2 (.a(A_input), .b({32{1'b0}}), .gt(out_4), .eq(out_5), .lt(out_6));
  assign or_1_out = A_input | B_input;  // OR_Gate or_1, 32 bits wide
  // Probe on ALU_Result
  Multiplexer #(.select(2), .width(32), .enable("false")) multiplexer_1 (
    .in0(or_1_out), .in1(adder_1_out), .in2(subtractor_1_out), .in3(controlled_buffer_1_out),
    .out(ALU_Result), .sel(OP));
endmodule

module Decode_Stage (
  input  [31:0] Instruction,
  output [5:0] out_2,
  output [3:0] out_3,
  output [3:0] out_4,
  output [3:0] out_5,
  output [13:0] out_6
);


  assign out_2 = Instruction[31:26];
  assign out_3 = Instruction[25:22];
  assign out_4 = Instruction[21:18];
  assign out_5 = Instruction[17:14];
  assign out_6 = Instruction[13:0];

  // Other names for the same wires on the sheet: Imm14[13:0] = Instruction[13:0]; Rt[3:0] = Instruction[17:14];
  //   Rs[3:0] = Instruction[21:18]; Rd[3:0] = Instruction[25:22]; OP[5:0] = Instruction[31:26]
endmodule

module Mem_WB (
  input  [3:0] Rd,
  input  [31:0] Data,
  input  WB,
  input  Clk_prime,
  input  in_5,
  output [3:0] Rd_2,
  output [31:0] Data_2,
  output WB_2
);

  Register #(.width(4)) u_Rd (.D(Rd), .Q(Rd_2), .clk(Clk_prime), .clr(in_5));  // open: en
  Register #(.width(32)) u_Data (.D(Data), .Q(Data_2), .clk(Clk_prime), .clr(in_5));  // open: en
  Register #(.width(1)) u_WB (.D(WB), .Q(WB_2), .clk(Clk_prime), .clr(in_5));  // open: en
endmodule

module ID_Mem (
  input  [3:0] Rd,
  input  [1:0] WB,
  input  MEM_Red,
  input  MEM_Write,
  input  [31:0] inp_1,
  input  [31:0] inp_2,
  input  [31:0] Data,
  input  [1:0] Alu_Signal,
  input  WE,
  input  [19:0] Pc,
  input  CLK,
  input  in_12,
  output [3:0] Rd_2,
  output [1:0] WB_2,
  output MEM_Red_2,
  output MEM_Write_2,
  output [31:0] inp_1_2,
  output [31:0] inp_2_2,
  output [31:0] Data_2,
  output [1:0] Alu_Signal_2,
  output WE_2,
  output [19:0] Pc_2
);

  Register #(.width(4)) register_1 (.D(Rd), .Q(Rd_2), .clk(CLK), .clr(in_12));  // open: en
  Register #(.width(2)) register_2 (.D(WB), .Q(WB_2), .clk(CLK), .clr(in_12));  // open: en
  Register #(.width(1)) register_3 (.D(MEM_Red), .Q(MEM_Red_2), .clk(CLK), .clr(in_12));  // open: en
  Register #(.width(1)) register_4 (.D(MEM_Write), .Q(MEM_Write_2), .clk(CLK), .clr(in_12));  // open: en
  Register #(.width(32)) register_5 (.D(inp_1), .Q(inp_1_2), .clk(CLK), .clr(in_12));  // open: en
  Register #(.width(32)) register_6 (.D(inp_2), .Q(inp_2_2), .clk(CLK), .clr(in_12));  // open: en
  Register #(.width(32)) register_7 (.D(Data), .Q(Data_2), .clk(CLK), .clr(in_12));  // open: en
  Register #(.width(2)) register_8 (.D(Alu_Signal), .Q(Alu_Signal_2), .clk(CLK), .clr(in_12));  // open: en
  Register #(.width(1)) register_9 (.D(WE), .Q(WE_2), .clk(CLK), .clr(in_12));  // open: en
  Register #(.width(20)) register_10 (.D(Pc), .Q(Pc_2), .clk(CLK), .clr(in_12));  // open: en
endmodule

module EX_Mem (
  input  [3:0] Rd,
  input  WE,
  input  Mem_Read,
  input  Mem_Write,
  input  [31:0] Result,
  input  [31:0] Data,
  input  C,
  input  eq,
  input  B,
  input  [1:0] WB,
  input  [19:0] Pc,
  input  CLK,
  input  in_13,
  output [3:0] Rd_2,
  output WE_2,
  output Mem_Read_2,
  output Mem_Write_2,
  output [31:0] Result_2,
  output [31:0] Data_2,
  output C_2,
  output eq_2,
  output B_2,
  output [1:0] WB_2,
  output [19:0] Pc_2
);

  Register #(.width(4)) register_1 (.D(Rd), .Q(Rd_2), .clk(CLK), .clr(in_13));  // open: en
  Register #(.width(1)) register_2 (.D(WE), .Q(WE_2), .clk(CLK), .clr(in_13));  // open: en
  Register #(.width(1)) register_3 (.D(Mem_Read), .Q(Mem_Read_2), .clk(CLK), .clr(in_13));  // open: en
  Register #(.width(1)) register_4 (.D(Mem_Write), .Q(Mem_Write_2), .clk(CLK), .clr(in_13));  // open: en
  Register #(.width(32)) register_5 (.D(Result), .Q(Result_2), .clk(CLK), .clr(in_13));  // open: en
  Register #(.width(32)) register_6 (.D(Data), .Q(Data_2), .clk(CLK), .clr(in_13));  // open: en
  Register #(.width(1)) register_7 (.D(C), .Q(C_2), .clk(CLK), .clr(in_13));  // open: en
  Register #(.width(1)) register_8 (.D(eq), .Q(eq_2), .clk(CLK), .clr(in_13));  // open: en
  Register #(.width(1)) register_9 (.D(B), .Q(B_2), .clk(CLK), .clr(in_13));  // open: en
  Register #(.width(2)) register_10 (.D(WB), .Q(WB_2), .clk(CLK), .clr(in_13));  // open: en
  Register #(.width(20)) register_11 (.D(Pc), .Q(Pc_2), .clk(CLK), .clr(in_13));  // open: en
endmodule

module IF_Mem (
  input  [31:0] Inst,
  input  [19:0] Pc,
  input  CLK,
  input  in_4,
  output [31:0] Inst_2,
  output [19:0] Pc_2
);

  Register #(.width(32)) register_1 (.D(Inst), .Q(Inst_2), .clk(CLK), .clr(in_4));  // open: en
  Register #(.width(20)) register_2 (.D(Pc), .Q(Pc_2), .clk(CLK), .clr(in_4));  // open: en
endmodule

module Forwarding_Unit (
  input  [3:0] Rs,
  input  [3:0] Rd_EX,
  input  [3:0] Rd_MEM,
  input  [3:0] Rd_WB,
  input  EX_WE,
  input  Mem_WE,
  input  WB_WE,
  output [1:0] Forward
);

  wire and_1_out, and_2_out, and_3_out, and_4_out, and_5_out, and_6_out, comparator_1_eq, comparator_2_eq,
       comparator_3_eq, not_1_out, not_2_out;

  Comparator #(.width(4)) comparator_1 (.a(Rs), .b(Rd_EX), .eq(comparator_1_eq));  // open: gt, lt
  Comparator #(.width(4)) comparator_2 (.a(Rs), .b(Rd_MEM), .eq(comparator_2_eq));  // open: gt, lt
  Comparator #(.width(4)) comparator_3 (.a(Rs), .b(Rd_WB), .eq(comparator_3_eq));  // open: gt, lt
  and and_1 (and_1_out, comparator_3_eq, WB_WE);
  and and_2 (and_2_out, comparator_1_eq, EX_WE);
  and and_3 (and_3_out, comparator_2_eq, Mem_WE);
  not not_1 (not_1_out, and_3_out);
  not not_2 (not_2_out, and_2_out);
  and and_4 (and_4_out, not_1_out, and_1_out);
  and and_5 (and_5_out, not_2_out, and_3_out);
  and and_6 (and_6_out, not_2_out, and_1_out);
  or S1 (Forward[1], and_5_out, and_6_out);
  or S0 (Forward[0], and_2_out, and_4_out);
endmodule

module Stall_Detection (
  input  MEMREAD_EX,
  input  [1:0] FORWARD_A,
  input  [1:0] FORWARD_B,
  output Stall
);

  wire comparator_1_eq, comparator_2_eq, or_1_out;

  Comparator #(.width(2)) comparator_1 (.a(2'b01), .b(FORWARD_A), .eq(comparator_1_eq));  // open: gt, lt
  Comparator #(.width(2)) comparator_2 (.a(2'b01), .b(FORWARD_B), .eq(comparator_2_eq));  // open: gt, lt
  or or_1 (or_1_out, comparator_1_eq, comparator_2_eq);
  and and_1 (Stall, MEMREAD_EX, or_1_out);
endmodule

module Kill_Detection (
  input  [5:0] Op,
  input  eq,
  input  C,
  input  B,
  output KILL
);

  wire and_1_out, and_2_out, and_3_out, comparator_1_eq, comparator_2_eq, comparator_3_eq, comparator_4_eq,
       comparator_5_eq, comparator_6_eq;

  Comparator #(.width(6)) comparator_1 (.a(Op), .b(6'b001010), .eq(comparator_1_eq));  // open: gt, lt
  Comparator #(.width(6)) comparator_2 (.a(6'b001101), .b(Op), .eq(comparator_2_eq));  // open: gt, lt
  Comparator #(.width(6)) comparator_3 (.a(6'b001110), .b(Op), .eq(comparator_3_eq));  // open: gt, lt
  Comparator #(.width(6)) comparator_4 (.a(6'b001111), .b(Op), .eq(comparator_4_eq));  // open: gt, lt
  Comparator #(.width(6)) comparator_5 (.a(Op), .b(6'b001011), .eq(comparator_5_eq));  // open: gt, lt
  Comparator #(.width(6)) comparator_6 (.a(Op), .b(6'b001100), .eq(comparator_6_eq));  // open: gt, lt
  and and_1 (and_1_out, comparator_1_eq, eq);
  and and_2 (and_2_out, B, comparator_6_eq);
  and and_3 (and_3_out, C, comparator_5_eq);
  or or_1 (KILL, and_1_out, and_3_out, and_2_out, comparator_2_eq, comparator_3_eq, comparator_4_eq);

  // Notes on the sheet:
  //   bgz
  //   blz
  //   bz
endmodule

module Hazard_Detection (
  input  MEMRead_EX,
  input  [1:0] FA,
  input  [1:0] FB,
  input  [5:0] in_4,
  input  in_5,
  input  in_6,
  input  in_7,
  output Stall,
  output out_9
);

  Stall_Detection stall_detection_1 (.MEMREAD_EX(MEMRead_EX), .FORWARD_A(FB), .FORWARD_B(FA), .Stall(Stall));
  Kill_Detection kill_detection_1 (.Op(in_4), .eq(in_5), .C(in_6), .B(in_7), .KILL(out_9));
endmodule

module LDW (
  input  [5:0] in_1,
  input  Clock,
  output Round2_Load,
  output Round2_Store
);

  wire _0p8, _0p9, and_1_out, and_2_out, and_3_out, and_4_out, buffer_1_out, buffer_2_out, buffer_3_out,
       j_k_ff_1_q, j_k_ff_2_q, not_1_out, not_2_out, not_3_out, not_4_out, not_5_out, not_6_out, not_7_out,
       not_8_out, not_9_out, not_10_out, not_11_out, not_12_out, not_13_out, not_14_out, not_15_out, o8, o9;

  and and_1 (and_1_out, Clock, and_3_out);
  and and_2 (and_2_out, and_4_out, Clock);
  buf buffer_1 (buffer_1_out, in_1[0]);
  not not_1 (not_1_out, in_1[1]);
  not not_2 (not_2_out, in_1[2]);
  buf buffer_2 (buffer_2_out, in_1[3]);
  not not_3 (not_3_out, in_1[4]);
  not not_4 (not_4_out, in_1[5]);
  J_K_Flip_Flop #(.trigger("falling")) j_k_ff_1 (
    .J(1'b1), .clk(and_1_out), .K(1'b1), .Q(j_k_ff_1_q), .reset(not_11_out));  // open: Qn, preset, en
  J_K_Flip_Flop #(.trigger("falling")) j_k_ff_2 (
    .J(1'b1), .clk(and_2_out), .K(1'b1), .Q(j_k_ff_2_q), .reset(not_5_out));  // open: Qn, preset, en
  not not_5 (not_5_out, and_4_out);
  not not_6 (not_6_out, in_1[0]);
  not not_7 (not_7_out, in_1[1]);
  not not_8 (not_8_out, in_1[2]);
  buf buffer_3 (buffer_3_out, in_1[3]);
  not not_9 (not_9_out, in_1[4]);
  not not_10 (not_10_out, in_1[5]);
  not not_11 (not_11_out, and_3_out);
  and and_3 (and_3_out, not_6_out, not_7_out, not_8_out, buffer_3_out, not_9_out, not_10_out);
  and and_4 (and_4_out, buffer_1_out, not_1_out, not_2_out, buffer_2_out, not_3_out, not_4_out);
  xor xor_1 (_0p8, and_3_out, Round2_Load);
  xor xor_2 (_0p9, and_4_out, Round2_Store);
  not not_12 (not_12_out, j_k_ff_1_q);
  not not_13 (not_13_out, j_k_ff_2_q);
  D_Flip_Flop d_ff_1 (.clk(Clock), .D(o8), .Q(Round2_Load), .reset(not_15_out));  // open: Qn, preset, en
  D_Flip_Flop d_ff_2 (.clk(Clock), .D(o9), .Q(Round2_Store), .reset(not_14_out));  // open: Qn, preset, en
  not not_14 (not_14_out, and_4_out);
  not not_15 (not_15_out, and_3_out);
  and and_5 (o9, _0p9, not_12_out);
  and and_6 (o8, _0p8, not_13_out);
endmodule
